// Digital circuit RV5-CSR.dig as structural Verilog
module RV5_CSR (
  input  clk,
  input  [11:0] addr,
  input  [31:0] w_data,
  input  wen,
  input  [31:0] pc_in,
  input  ecall_sel,
  input  mret_sel,
  output [31:0] R_DATA,
  output [31:0] MTVEC_OUT,
  output [31:0] MEPC_OUT
);

  wire and_1_out, and_2_out, and_3_out, and_4_out, and_5_out, mcause_sel, mepc_sel, mscratch_sel,
       mstatus_sel, mtvec_sel, or_1_out, or_2_out;
  wire [2:0] priorityencoder_1_num;
  wire [31:0] mcause_q, mscratch_q, mstatus_q, multiplexer_1_out, multiplexer_2_out;

  Comparator #(.Bits(12)) comparator_1 (.a(addr), .b(12'h300), .eq(mstatus_sel));  // open: gt, lt
  Comparator #(.Bits(12)) comparator_2 (.a(addr), .b(12'h305), .eq(mtvec_sel));  // open: gt, lt
  Comparator #(.Bits(12)) comparator_3 (.a(addr), .b(12'h340), .eq(mscratch_sel));  // open: gt, lt
  Comparator #(.Bits(12)) comparator_4 (.a(addr), .b(12'h341), .eq(mepc_sel));  // open: gt, lt
  Comparator #(.Bits(12)) comparator_5 (.a(addr), .b(12'h342), .eq(mcause_sel));  // open: gt, lt
  Multiplexer #(.Bits(32)) multiplexer_1 (.sel(ecall_sel), .in_0(w_data), .in_1(pc_in), .out(multiplexer_1_out));
  Multiplexer #(.Bits(32)) multiplexer_2 (.sel(ecall_sel), .in_0(w_data), .in_1(32'hb), .out(multiplexer_2_out));
  and and_1 (and_1_out, wen, mepc_sel);
  and and_2 (and_2_out, wen, mcause_sel);
  and and_3 (and_3_out, wen, mstatus_sel);
  and and_4 (and_4_out, wen, mtvec_sel);
  and and_5 (and_5_out, wen, mscratch_sel);
  or or_1 (or_1_out, and_1_out, ecall_sel);
  or or_2 (or_2_out, and_2_out, ecall_sel);
  Register #(.Bits(32)) mstatus (.D(w_data), .C(clk), .en(and_3_out), .Q(mstatus_q));
  Register #(.Bits(32)) mtvec (.D(w_data), .C(clk), .en(and_4_out), .Q(MTVEC_OUT));
  Register #(.Bits(32)) mscratch (.D(w_data), .C(clk), .en(and_5_out), .Q(mscratch_q));
  Register #(.Bits(32)) mepc (.D(multiplexer_1_out), .C(clk), .en(or_1_out), .Q(MEPC_OUT));
  Register #(.Bits(32)) mcause (.D(multiplexer_2_out), .C(clk), .en(or_2_out), .Q(mcause_q));
  PriorityEncoder #(.Selector_Bits(3)) priorityencoder_1 (
    .in0(mstatus_sel), .in1(mtvec_sel), .in2(mscratch_sel), .in3(mepc_sel), .in4(mcause_sel), .in5(1'b0),
    .in6(1'b0), .in7(1'b0), .num(priorityencoder_1_num));  // open: any
  Multiplexer #(.Selector_Bits(3), .Bits(32)) multiplexer_3 (
    .sel(priorityencoder_1_num), .in_0(mstatus_q), .in_1(MTVEC_OUT), .in_2(mscratch_q), .in_3(MEPC_OUT),
    .in_4(mcause_q), .in_5({32{1'b0}}), .in_6({32{1'b0}}), .in_7({32{1'b0}}), .out(R_DATA));

  // Notes on the sheet:
  //   RV5-CSR
endmodule
