// Digital circuit RV5-MAIN-CONTROL.dig as structural Verilog
module RV5_MAIN_CONTROL (
  input  [6:0] opcode,
  output [1:0] wb_sel,
  output ram_wen,
  output ram_ren,
  output reg_wen,
  output branch_sel,
  output jal_sel,
  output jalr_sel,
  output [1:0] alu_asel,
  output alu_bsel,
  output [2:0] imm_sel,
  output [1:0] alu_opclass
);

  FROMTRUTH6 fromtruth6_1 (
    .op6(opcode[6]), .op5(opcode[5]), .op4(opcode[4]), .op3(opcode[3]), .op2(opcode[2]),
    .wb_sel_1(wb_sel[1]), .wb_sel_0(wb_sel[0]), .ram_wen(ram_wen), .ram_ren(ram_ren), .reg_wen(reg_wen),
    .branch_sel(branch_sel), .jal_sel(jal_sel), .jalr_sel(jalr_sel), .alu_asel_1(alu_asel[1]),
    .alu_asel_0(alu_asel[0]), .alu_bsel(alu_bsel), .imm_sel_2(imm_sel[2]), .imm_sel_1(imm_sel[1]),
    .imm_sel_0(imm_sel[0]), .alu_op_class_1(alu_opclass[1]), .alu_op_class_0(alu_opclass[0]));

  // Notes on the sheet:
  //   RV5-MAIN-CONTROL
endmodule
