// Digital circuit RV5-MEM-CONTROL.dig as structural Verilog
module RV5_MEM_CONTROL (
  input  [2:0] funct3,
  output ram_b,
  output ram_h,
  output ld_signext
);

  wire not_2_out;

  not not_1 (ld_signext, funct3[2]);
  nor nor_1 (ram_b, funct3[0], funct3[1]);
  not not_2 (not_2_out, funct3[1]);
  and and_1 (ram_h, funct3[0], not_2_out);

  // Notes on the sheet:
  //   RV5-MEM-CONTROL
endmodule
