// Digital circuit RV5-MEMORY.dig as structural Verilog
module RV5_MEMORY (
  input  [31:0] addr,
  input  [31:0] din,
  input  wen,
  input  ren,
  input  clk,
  input  \byte ,
  input  half,
  input  signext,
  output [31:0] out
);

  wire addr_ram, addr_terminal, and_1_out, and_2_out, and_3_out, decoder_1_out_1, decoder_1_out_2,
       decoder_1_out_3, multiplexer_1_out, multiplexer_2_out, multiplexer_3_out, wb0, wb1, wb2, wb3;
  wire [7:0] multiplexer_8_out, multiplexer_8_out_2, multiplexer_8_out_3, multiplexer_8_out_4,
       multiplexer_9_out, multiplexer_10_out, multiplexer_11_out, multiplexer_12_out, ob0, ob1, ob2, ob3,
       rv5_srl_1_out;
  wire [15:8] rv5_srl_1_out_2;
  wire [31:0] bitextender_1_out, bitextender_2_out, multiplexer_4_out, multiplexer_13_out,
       multiplexer_14_out, multiplexer_15_out, RAM_d1;
  wire [31:16] rv5_srl_1_out_3;

  Decoder #(.Selector_Bits(2)) decoder_1 (
    .sel(addr[1:0]), .out_0(wb0), .out_1(decoder_1_out_1), .out_2(decoder_1_out_2), .out_3(decoder_1_out_3));
  Multiplexer multiplexer_1 (.sel(half), .in_0(wb0), .in_1(wb0), .out(multiplexer_1_out));
  Multiplexer multiplexer_2 (.sel(half), .in_0(wb0), .in_1(decoder_1_out_2), .out(multiplexer_2_out));
  Multiplexer multiplexer_3 (.sel(half), .in_0(wb0), .in_1(decoder_1_out_2), .out(multiplexer_3_out));
  and and_1 (and_1_out, addr_terminal, wen);
  Comparator #(.Bits(32)) comparator_1 (.a(addr), .b(32'h1000), .eq(addr_terminal), .lt(addr_ram));  // open: gt
  Multiplexer #(.Bits(32)) multiplexer_4 (
    .sel(\byte ), .in_0(din), .in_1({din[7:0], din[7:0], din[7:0], din[7:0]}), .out(multiplexer_4_out));
  Multiplexer multiplexer_5 (.sel(\byte ), .in_0(multiplexer_1_out), .in_1(decoder_1_out_1), .out(wb1));
  Multiplexer multiplexer_6 (.sel(\byte ), .in_0(multiplexer_2_out), .in_1(decoder_1_out_2), .out(wb2));
  Multiplexer multiplexer_7 (.sel(\byte ), .in_0(multiplexer_3_out), .in_1(decoder_1_out_3), .out(wb3));
  Terminal terminal_1 (.D(din), .C(clk), .en(and_1_out));
  Multiplexer #(.Bits(32)) multiplexer_8 (
    .sel(half), .in_0(multiplexer_4_out), .in_1({din[15:0], din[15:0]}),
    .out({multiplexer_8_out_4, multiplexer_8_out_3, multiplexer_8_out_2, multiplexer_8_out}));
  and and_2 (and_2_out, wen, addr_ram);
  and and_3 (and_3_out, ren, addr_ram);
  Multiplexer #(.Bits(8)) multiplexer_9 (.sel(wb0), .in_0(ob0), .in_1(multiplexer_8_out), .out(multiplexer_9_out));
  Multiplexer #(.Bits(8)) multiplexer_10 (.sel(wb1), .in_0(ob1), .in_1(multiplexer_8_out_2), .out(multiplexer_10_out));
  Multiplexer #(.Bits(8)) multiplexer_11 (.sel(wb2), .in_0(ob2), .in_1(multiplexer_8_out_3), .out(multiplexer_11_out));
  Multiplexer #(.Bits(8)) multiplexer_12 (.sel(wb3), .in_0(ob3), .in_1(multiplexer_8_out_4), .out(multiplexer_12_out));
  RAMDualAccess #(.AddrBits(10), .isProgramMemory("true"), .Bits(32)) RAM (
    .str(and_2_out), .C(clk), .ld(and_3_out), .A1(addr[11:2]),
    .Din1({multiplexer_12_out, multiplexer_11_out, multiplexer_10_out, multiplexer_9_out}), .A2(addr[11:2]),
    .D1(RAM_d1), .D2({ob3, ob2, ob1, ob0}));
  RV5_SRL rv5_srl_1 (.in(RAM_d1), .shift({addr[1:0], 3'b000}), .out({rv5_srl_1_out_3, rv5_srl_1_out_2, rv5_srl_1_out}));
  BitExtender #(.inputBits(16), .outputBits(32)) bitextender_1 (
    .in({rv5_srl_1_out_2, rv5_srl_1_out}), .out(bitextender_1_out));
  BitExtender #(.outputBits(32)) bitextender_2 (.in(rv5_srl_1_out), .out(bitextender_2_out));
  Multiplexer #(.Bits(32)) multiplexer_13 (
    .sel(signext), .in_0({{16{1'b0}}, rv5_srl_1_out_2, rv5_srl_1_out}), .in_1(bitextender_1_out),
    .out(multiplexer_13_out));
  Multiplexer #(.Bits(32)) multiplexer_14 (
    .sel(signext), .in_0({{24{1'b0}}, rv5_srl_1_out}), .in_1(bitextender_2_out), .out(multiplexer_14_out));
  Multiplexer #(.Bits(32)) multiplexer_15 (
    .sel(\byte ), .in_0({rv5_srl_1_out_3, rv5_srl_1_out_2, rv5_srl_1_out}), .in_1(multiplexer_14_out),
    .out(multiplexer_15_out));
  Multiplexer #(.Bits(32)) multiplexer_16 (.sel(half), .in_0(multiplexer_15_out), .in_1(multiplexer_13_out), .out(out));

  // Other names for the same wires on the sheet: b = \byte ; h = half; ram_addr[31:0] = addr; ram_din[31:0] = din;
  //   ram_ren = ren; ram_signext = signext; ram_wen = wen

  // Notes on the sheet:
  //   If we're storing a byte or a half,
  //   copy the value into all slots.
  //   Determine which bytes should
  //   be overwritten.
  //   Mix the old bytes with the
  //   new ones.
  //   Shift our output so 
  //   what we want
  //   starts at LSB.
  //   Handle optional sign extension
  //   for all read sizes.
endmodule
