// Digital circuit RV5-PCU.dig as structural Verilog
module RV5_PCU (
  input  [31:0] IMM_32,
  input  CLK,
  input  IS_BRANCH,
  input  IS_JAL,
  input  IS_JALR,
  input  COND_MET,
  input  [31:0] ALU_OUT,
  input  IS_ECALL,
  input  [31:0] MTVEC,
  input  [31:0] MEPC,
  input  IS_MRET,
  input  IS_EBREAK,
  input  IS_DEBUG,
  input  [31:0] DCSR,
  input  [31:0] DPC,
  input  IS_DRET,
  input  HALTREQ,
  input  JUMPPROGBUF,
  input  RESUMEREQ,
  output [31:0] PC
);

  wire and_1_out, and_2_out, or_1_out, or_2_out, rising_edge_1_o;
  wire [3:0] priorityencoder_1_num;
  wire [29:0] multiplexer_1_out, multiplexer_2_out, multiplexer_3_out, PC_Incr_s;

  Register #(.Bits(30)) PC_w (.D(multiplexer_3_out), .C(CLK), .en(1'b1), .Q(PC[31:2]));
  and and_1 (and_1_out, IS_BRANCH, COND_MET);
  and and_2 (and_2_out, IS_DRET, IS_DEBUG);
  or or_1 (or_1_out, IS_JAL, and_1_out);
  RISING_EDGE rising_edge_1 (.clk(CLK), .d(RESUMEREQ), .o(rising_edge_1_o));
  Multiplexer #(.Bits(30)) multiplexer_1 (.sel(or_1_out), .in_0(30'h1), .in_1(IMM_32[31:2]), .out(multiplexer_1_out));
  Add #(.Bits(30)) PC_Incr (.a(PC[31:2]), .b(multiplexer_1_out), .c_i(1'b0), .s(PC_Incr_s));  // open: c_o
  or or_2 (or_2_out, IS_DEBUG, DCSR[15]);
  Multiplexer #(.Bits(30)) multiplexer_2 (.sel(or_2_out), .in_0(MTVEC[31:2]), .in_1(30'h64), .out(multiplexer_2_out));
  PriorityEncoder #(.Selector_Bits(4)) priorityencoder_1 (
    .in0(1'b0), .in1(IS_JALR), .in2(IS_ECALL), .in3(IS_MRET), .in4(IS_EBREAK), .in5(and_2_out),
    .in6(HALTREQ), .in7(JUMPPROGBUF), .in8(rising_edge_1_o), .in9(1'b0), .in10(1'b0), .in11(1'b0),
    .in12(1'b0), .in13(1'b0), .in14(1'b0), .in15(1'b0), .num(priorityencoder_1_num));  // open: any
  Multiplexer #(.Selector_Bits(4), .Bits(30)) multiplexer_3 (
    .sel(priorityencoder_1_num), .in_0(PC_Incr_s), .in_1(ALU_OUT[31:2]), .in_2(MTVEC[31:2]),
    .in_3(MEPC[31:2]), .in_4(multiplexer_2_out), .in_5(DPC[31:2]), .in_6(30'h64), .in_7(30'h401),
    .in_8(30'h65), .in_9({30{1'b0}}), .in_10({30{1'b0}}), .in_11({30{1'b0}}), .in_12({30{1'b0}}),
    .in_13({30{1'b0}}), .in_14({30{1'b0}}), .in_15({30{1'b0}}), .out(multiplexer_3_out));

  assign PC[1:0] = 2'b00;

  // Other names for the same wires on the sheet: sgn_ext_imm32[31:0] = IMM_32

  // Notes on the sheet:
  //   PCU(Program Control Unit)
  //   IMM_32 should probably be replaced 
  //   with sgn-ext-imm32 from RV5-IMM
  //   PC = PC + 4, or PC = PC += SBimm32
  //   or PC = ALU out or PC += sgn_ext-imm32
  //   for FMT U, and UJ
  //   /30
endmodule
