// Digital circuit RV5-ALU.dig as structural Verilog
module RV5_ALU (
  input  [2:0] OP,
  input  [31:0] A,
  input  [31:0] B,
  input  SUB,
  output [31:0] Y,
  output EQ,
  output SLT,
  output CRY
);

  wire sgt;
  wire [0:0] not_2_out;
  wire [31:0] \and , multiplexer_1_out, not_1_out, \or , sll, sr, sra_1_out, srl_1_out, sum, \xor ;

  assign not_1_out = ~B;  // Not not_1, 32 bits wide
  Multiplexer #(.Bits(32)) multiplexer_1 (.sel(SUB), .in_0(B), .in_1(not_1_out), .out(multiplexer_1_out));
  SLL sll_1 (.in(A), .shift(B[4:0]), .out(sll));
  SRL srl_1 (.in(A), .shift(B[4:0]), .out(srl_1_out));
  SRA sra_1 (.in(A), .shift(B[4:0]), .out(sra_1_out));
  Comparator #(.Signed("true"), .Bits(32)) comparator_1 (.a(A), .b(B), .gt(sgt), .eq(EQ), .lt(SLT));
  Add #(.Bits(32)) add_1 (.a(A), .b(multiplexer_1_out), .c_i(SUB), .s(sum), .c_o(CRY));
  Multiplexer #(.Bits(32)) multiplexer_2 (.sel(SUB), .in_0(srl_1_out), .in_1(sra_1_out), .out(sr));
  assign \or  = A | B;  // Or or_1, 32 bits wide
  assign \xor  = A ^ B;  // XOr xor_1, 32 bits wide
  assign \and  = A & B;  // And and_1, 32 bits wide
  not not_2 (not_2_out[0], CRY);
  Multiplexer #(.Selector_Bits(3), .Bits(32)) multiplexer_3 (
    .sel(OP), .in_0(sum), .in_1(sll), .in_2({{31{1'b0}}, SLT}), .in_3({{31{1'b0}}, not_2_out[0]}),
    .in_4(\xor ), .in_5(sr), .in_6(\or ), .in_7(\and ), .out(Y));

  // Other names for the same wires on the sheet: carry = CRY

  // Notes on the sheet:
  //   RV-ALU : Combinational
  //   TODO: DOC
endmodule
