// Digital circuit RV5-BRANCH-CONTROL.dig as structural Verilog
module RV5_BRANCH_CONTROL (
  input  is_branch,
  input  [2:0] funct3,
  output branch_sel,
  output alu_mod,
  output [2:0] alu_op,
  output [2:0] imm_sel
);

  Multiplexer #(.Bits(3)) multiplexer_1 (.sel(is_branch), .in_0(3'b000), .in_1(funct3), .out(alu_op));
  Multiplexer #(.Bits(3)) multiplexer_2 (.sel(is_branch), .in_0(3'b000), .in_1(3'b010), .out(imm_sel));

  assign alu_mod = is_branch;
  assign branch_sel = is_branch;

  // Notes on the sheet:
  //   RV5-BRANCH-CONTROL
  //   TODO: DOC
endmodule
