// Digital circuit RV5-MEMORY.dig as structural Verilog
module RV5_MEMORY (
  input  [31:0] addr,
  input  [31:0] wdata,
  input  wen,
  input  ren,
  input  clk,
  input  \byte ,
  input  half,
  input  signext,
  input  [31:0] addr_inst,
  input  [31:0] addr_dm,
  input  wen_dm,
  input  [31:0] wdata_dm,
  output [31:0] out,
  output [31:0] out_inst,
  output [31:0] out_dm
);

  wire addr_data0, addr_dm_data0, addr_dm_progbuf_0, addr_dm_progbuf_1, addr_dm_progbuf_2, addr_dm_progbuf_3,
       addr_dm_progbuf_4, addr_dm_progbuf_5, addr_dm_progbuf_6, addr_dm_progbuf_7, addr_filemap,
       addr_inst_data0, addr_inst_filemap, addr_inst_progbuf_0, addr_inst_progbuf_1, addr_inst_progbuf_2,
       addr_inst_progbuf_3, addr_inst_progbuf_4, addr_inst_progbuf_5, addr_inst_progbuf_6,
       addr_inst_progbuf_7, addr_inst_ram, addr_inst_terminal, addr_progbuf_0, addr_progbuf_1,
       addr_progbuf_2, addr_progbuf_3, addr_progbuf_4, addr_progbuf_5, addr_progbuf_6, addr_progbuf_7,
       addr_ram, addr_terminal, and_1_out, and_2_out, and_3_out, and_4_out, and_5_out, and_6_out, and_7_out,
       and_8_out, and_9_out, and_10_out, and_11_out, and_12_out, and_13_out, and_14_out, and_15_out,
       and_16_out, comparator_2_lt, comparator_11_eq, comparator_11_lt, comparator_13_lt, comparator_22_eq,
       comparator_22_lt, interactiveterminal_1_p6, not_1_out, not_2_out, or_1_out, or_3_out, or_4_out,
       or_6_out;
  wire [3:0] addr_dm_range, addr_inst_range, addr_range;
  wire [15:0] interactiveterminal_1_p5, terminal;
  wire [31:0] data0, filemap, filemap_inst, filemapper_1_p7, masked_overlay_1_out, masked_overlay_2_out,
       multiplexer_2_out, progbuf_0, progbuf_1, progbuf_2, progbuf_3, progbuf_4, progbuf_5, progbuf_6,
       progbuf_7, ram, RAM_d1, ram_inst, sub_1_s, sub_2_s;

  MASKED_OVERLAY masked_overlay_1 (
    .base(RAM_d1), .data(wdata), .addr(addr), .\byte (\byte ), .half(half), .out(masked_overlay_1_out));
  and and_1 (and_1_out, wen, addr_ram);
  and and_2 (and_2_out, addr_terminal, wen);
  and and_3 (and_3_out, addr_terminal, ren);
  RAMDualAccess #(.AddrBits(24), .isProgramMemory("true"), .Bits(32)) u_RAM (
    .str(and_1_out), .C(clk), .ld(addr_ram), .A1(addr[25:2]), .Din1(masked_overlay_1_out),
    .A2(addr_inst[25:2]), .D1(RAM_d1), .D2(ram_inst));
  // InteractiveTerminal interactiveterminal_1: pin names not known; wires that end beside it: wdata, and_2_out, and_3_out, clk, interactiveterminal_1_p5, interactiveterminal_1_p6
  Comparator #(.Bits(32)) comparator_1 (.a(addr), .b(32'h418), .eq(addr_data0));  // open: gt, lt
  Comparator #(.Bits(32)) comparator_2 (.a(addr), .b(32'h10000), .eq(addr_terminal), .lt(comparator_2_lt));  // open: gt
  Comparator #(.Bits(32)) comparator_3 (.a(addr), .b(32'h10004), .eq(addr_progbuf_0));  // open: gt, lt
  Comparator #(.Bits(32)) comparator_4 (.a(addr), .b(32'h10008), .eq(addr_progbuf_1));  // open: gt, lt
  Comparator #(.Bits(32)) comparator_5 (.a(addr), .b(32'h1000c), .eq(addr_progbuf_2));  // open: gt, lt
  Comparator #(.Bits(32)) comparator_6 (.a(addr), .b(32'h10010), .eq(addr_progbuf_3));  // open: gt, lt
  Comparator #(.Bits(32)) comparator_7 (.a(addr), .b(32'h10014), .eq(addr_progbuf_4));  // open: gt, lt
  Comparator #(.Bits(32)) comparator_8 (.a(addr), .b(32'h10018), .eq(addr_progbuf_5));  // open: gt, lt
  Comparator #(.Bits(32)) comparator_9 (.a(addr), .b(32'h1001c), .eq(addr_progbuf_6));  // open: gt, lt
  Comparator #(.Bits(32)) comparator_10 (.a(addr), .b(32'h10020), .eq(addr_progbuf_7));  // open: gt, lt
  Comparator #(.Bits(32)) comparator_11 (
    .a(addr), .b(32'h3ffffff), .gt(addr_filemap), .eq(comparator_11_eq), .lt(comparator_11_lt));
  Multiplexer #(.Bits(16)) multiplexer_1 (
    .sel(interactiveterminal_1_p6), .in_0(16'h4), .in_1(interactiveterminal_1_p5), .out(terminal));
  not not_1 (not_1_out, addr_data0);
  ISOLATE_SIGNEXT isolate_signext_1 (
    .data(RAM_d1), .addr(addr), .want_byte(\byte ), .want_half(half), .signext(signext), .out(ram));
  and and_4 (and_4_out, not_1_out, comparator_2_lt);
  or or_1 (or_1_out, comparator_11_eq, comparator_11_lt);
  or or_2 (addr_ram, and_4_out, or_1_out);
  Comparator #(.Bits(32)) comparator_12 (.a(addr_inst), .b(32'h418), .eq(addr_inst_data0));  // open: gt, lt
  Comparator #(.Bits(32)) comparator_13 (
    .a(addr_inst), .b(32'h10000), .eq(addr_inst_terminal), .lt(comparator_13_lt));  // open: gt
  Comparator #(.Bits(32)) comparator_14 (.a(addr_inst), .b(32'h10004), .eq(addr_inst_progbuf_0));  // open: gt, lt
  Comparator #(.Bits(32)) comparator_15 (.a(addr_inst), .b(32'h10008), .eq(addr_inst_progbuf_1));  // open: gt, lt
  Comparator #(.Bits(32)) comparator_16 (.a(addr_inst), .b(32'h1000c), .eq(addr_inst_progbuf_2));  // open: gt, lt
  Comparator #(.Bits(32)) comparator_17 (.a(addr_inst), .b(32'h10010), .eq(addr_inst_progbuf_3));  // open: gt, lt
  Comparator #(.Bits(32)) comparator_18 (.a(addr_inst), .b(32'h10014), .eq(addr_inst_progbuf_4));  // open: gt, lt
  Comparator #(.Bits(32)) comparator_19 (.a(addr_inst), .b(32'h10018), .eq(addr_inst_progbuf_5));  // open: gt, lt
  Comparator #(.Bits(32)) comparator_20 (.a(addr_inst), .b(32'h1001c), .eq(addr_inst_progbuf_6));  // open: gt, lt
  Comparator #(.Bits(32)) comparator_21 (.a(addr_inst), .b(32'h10020), .eq(addr_inst_progbuf_7));  // open: gt, lt
  Comparator #(.Bits(32)) comparator_22 (
    .a(addr_inst), .b(32'h3ffffff), .gt(addr_inst_filemap), .eq(comparator_22_eq), .lt(comparator_22_lt));
  not not_2 (not_2_out, addr_inst_data0);
  Sub #(.Bits(32)) sub_1 (.a(addr), .b(32'h4000000), .c_i(1'b0), .s(sub_1_s));  // open: c_o
  Sub #(.Bits(32)) sub_2 (.a(addr_inst), .b(32'h4000000), .c_i(1'b0), .s(sub_2_s));  // open: c_o
  MASKED_OVERLAY masked_overlay_2 (
    .base(filemapper_1_p7), .data(wdata), .addr(addr), .\byte (\byte ), .half(half),
    .out(masked_overlay_2_out));
  and and_5 (and_5_out, addr_filemap, wen);
  or or_3 (or_3_out, addr_filemap, addr_inst_filemap);
  or or_4 (or_4_out, comparator_22_eq, comparator_22_lt);
  and and_6 (and_6_out, not_2_out, comparator_13_lt);
  or or_5 (addr_inst_ram, and_6_out, or_4_out);
  // FileMapper #(.Bits(32)) filemapper_1: pin names not known; wires that end beside it: {2'b00, sub_1_s[31:2]}, {2'b00, sub_2_s[31:2]}, masked_overlay_2_out, and_5_out, or_3_out, clk, filemapper_1_p7, filemap_inst
  Comparator #(.Bits(32)) comparator_23 (.a(addr_dm), .b(32'h418), .eq(addr_dm_data0));  // open: gt, lt
  Comparator #(.Bits(32)) comparator_24 (.a(addr_dm), .b(32'h10004), .eq(addr_dm_progbuf_0));  // open: gt, lt
  Comparator #(.Bits(32)) comparator_25 (.a(addr_dm), .b(32'h10008), .eq(addr_dm_progbuf_1));  // open: gt, lt
  Comparator #(.Bits(32)) comparator_26 (.a(addr_dm), .b(32'h1000c), .eq(addr_dm_progbuf_2));  // open: gt, lt
  Comparator #(.Bits(32)) comparator_27 (.a(addr_dm), .b(32'h10010), .eq(addr_dm_progbuf_3));  // open: gt, lt
  Comparator #(.Bits(32)) comparator_28 (.a(addr_dm), .b(32'h10014), .eq(addr_dm_progbuf_4));  // open: gt, lt
  Comparator #(.Bits(32)) comparator_29 (.a(addr_dm), .b(32'h10018), .eq(addr_dm_progbuf_5));  // open: gt, lt
  Comparator #(.Bits(32)) comparator_30 (.a(addr_dm), .b(32'h1001c), .eq(addr_dm_progbuf_6));  // open: gt, lt
  Comparator #(.Bits(32)) comparator_31 (.a(addr_dm), .b(32'h10020), .eq(addr_dm_progbuf_7));  // open: gt, lt
  ISOLATE_SIGNEXT isolate_signext_2 (
    .data(filemapper_1_p7), .addr(addr), .want_byte(\byte ), .want_half(half), .signext(signext),
    .out(filemap));
  and and_7 (and_7_out, addr_dm_progbuf_0, wen_dm);
  and and_8 (and_8_out, addr_dm_progbuf_1, wen_dm);
  and and_9 (and_9_out, addr_dm_progbuf_2, wen_dm);
  and and_10 (and_10_out, addr_dm_progbuf_3, wen_dm);
  and and_11 (and_11_out, addr_dm_progbuf_4, wen_dm);
  and and_12 (and_12_out, addr_dm_progbuf_5, wen_dm);
  and and_13 (and_13_out, addr_dm_progbuf_6, wen_dm);
  and and_14 (and_14_out, addr_dm_progbuf_7, wen_dm);
  and and_15 (and_15_out, addr_dm_data0, wen_dm);
  and and_16 (and_16_out, addr_data0, wen);
  Register #(.Bits(32)) u_progbuf_0 (.D(wdata_dm), .C(clk), .en(and_7_out), .Q(progbuf_0));
  Register #(.Bits(32)) u_progbuf_1 (.D(wdata_dm), .C(clk), .en(and_8_out), .Q(progbuf_1));
  Register #(.Bits(32)) u_progbuf_2 (.D(wdata_dm), .C(clk), .en(and_9_out), .Q(progbuf_2));
  Register #(.Bits(32)) u_progbuf_3 (.D(wdata_dm), .C(clk), .en(and_10_out), .Q(progbuf_3));
  Register #(.Bits(32)) u_progbuf_4 (.D(wdata_dm), .C(clk), .en(and_11_out), .Q(progbuf_4));
  Register #(.Bits(32)) u_progbuf_5 (.D(wdata_dm), .C(clk), .en(and_12_out), .Q(progbuf_5));
  Register #(.Bits(32)) u_progbuf_6 (.D(wdata_dm), .C(clk), .en(and_13_out), .Q(progbuf_6));
  Register #(.Bits(32)) u_progbuf_7 (.D(wdata_dm), .C(clk), .en(and_14_out), .Q(progbuf_7));
  Multiplexer #(.Bits(32)) multiplexer_2 (.sel(and_15_out), .in_0(wdata), .in_1(wdata_dm), .out(multiplexer_2_out));
  or or_6 (or_6_out, and_15_out, and_16_out);
  Register #(.Bits(32)) u_data0 (.D(multiplexer_2_out), .C(clk), .en(or_6_out), .Q(data0));
  PriorityEncoder #(.Selector_Bits(4)) priorityencoder_1 (
    .in0(1'b0), .in1(addr_ram), .in2(addr_terminal), .in3(addr_progbuf_0), .in4(addr_progbuf_1),
    .in5(addr_progbuf_2), .in6(addr_progbuf_3), .in7(addr_progbuf_4), .in8(addr_progbuf_5),
    .in9(addr_progbuf_6), .in10(addr_progbuf_7), .in11(addr_data0), .in12(addr_filemap), .in13(1'b0),
    .in14(1'b0), .in15(1'b0), .num(addr_range));  // open: any
  PriorityEncoder #(.Selector_Bits(4)) priorityencoder_2 (
    .in0(1'b0), .in1(addr_inst_ram), .in2(addr_inst_terminal), .in3(addr_inst_progbuf_0),
    .in4(addr_inst_progbuf_1), .in5(addr_inst_progbuf_2), .in6(addr_inst_progbuf_3),
    .in7(addr_inst_progbuf_4), .in8(addr_inst_progbuf_5), .in9(addr_inst_progbuf_6),
    .in10(addr_inst_progbuf_7), .in11(addr_inst_data0), .in12(addr_inst_filemap), .in13(1'b0), .in14(1'b0),
    .in15(1'b0), .num(addr_inst_range));  // open: any
  PriorityEncoder #(.Selector_Bits(4)) priorityencoder_3 (
    .in0(1'b0), .in1(1'b0), .in2(1'b0), .in3(addr_dm_progbuf_0), .in4(addr_dm_progbuf_1),
    .in5(addr_dm_progbuf_2), .in6(addr_dm_progbuf_3), .in7(addr_dm_progbuf_4), .in8(addr_dm_progbuf_5),
    .in9(addr_dm_progbuf_6), .in10(addr_dm_progbuf_7), .in11(addr_dm_data0), .in12(1'b0), .in13(1'b0),
    .in14(1'b0), .in15(1'b0), .num(addr_dm_range));  // open: any
  Multiplexer #(.Selector_Bits(4), .Bits(32)) multiplexer_3 (
    .sel(addr_range), .in_0({32{1'b0}}), .in_1(ram), .in_2({{16{1'b0}}, terminal}), .in_3(progbuf_0),
    .in_4(progbuf_1), .in_5(progbuf_2), .in_6(progbuf_3), .in_7(progbuf_4), .in_8(progbuf_5),
    .in_9(progbuf_6), .in_10(progbuf_7), .in_11(data0), .in_12(filemap), .in_13({32{1'b0}}),
    .in_14({32{1'b0}}), .in_15({32{1'b0}}), .out(out));
  Multiplexer #(.Selector_Bits(4), .Bits(32)) multiplexer_4 (
    .sel(addr_dm_range), .in_0({32{1'b0}}), .in_1({32{1'b0}}), .in_2({32{1'b0}}), .in_3(progbuf_0),
    .in_4(progbuf_1), .in_5(progbuf_2), .in_6(progbuf_3), .in_7(progbuf_4), .in_8(progbuf_5),
    .in_9(progbuf_6), .in_10(progbuf_7), .in_11(data0), .in_12({32{1'b0}}), .in_13({32{1'b0}}),
    .in_14({32{1'b0}}), .in_15({32{1'b0}}), .out(out_dm));
  Multiplexer #(.Selector_Bits(4), .Bits(32)) multiplexer_5 (
    .sel(addr_inst_range), .in_0({32{1'b0}}), .in_1(ram_inst), .in_2({32{1'b0}}), .in_3(progbuf_0),
    .in_4(progbuf_1), .in_5(progbuf_2), .in_6(progbuf_3), .in_7(progbuf_4), .in_8(progbuf_5),
    .in_9(progbuf_6), .in_10(progbuf_7), .in_11(data0), .in_12(filemap_inst), .in_13({32{1'b0}}),
    .in_14({32{1'b0}}), .in_15({32{1'b0}}), .out(out_inst));

  // Notes on the sheet:
  //   RV5-MEMORY
  //   Inputs
  //   All of our inputs!
  //   Memory-Mapped Items
  //   RAM
  //   Terminal
  //   This is a dual-port RAM. It supports reading and writing at address 1A
  //   and reading at address 1B. I'm using 1A for instruction operations and
  //   1B for instruction reads.
  //   If we're writing a half or byte, we
  //   need to take the remaining bytes
  //   of the old word and merge them
  //   with our new bytes.
  //   This is the terminal! We can read and write characters! Character input
  //   is queued, and a value of 4 (EOT in ASCII) means there is currently
  //   nothing left.
  //   Address Control Signals
  //   We determine which devices are currently being addressed.
  //   We might need to sign extend.
  //   Additionally, if we're reading a byte
  //   or a half, we need to isolate that
  //   value from the rest of the word.
  //   Mapped File
  //   This component has an interface for controlling file mapping (at relative
  //   address 0x0) and potentially a mapped file (at relative address 0x1000).
  //   The contents can be executed.
  //   TODO: Simplify logic
  //   Program Buffer
  //   data0
  //   Understanding the Memory
  //   This is a memory module with a few items mapped. Of course,
  //   we have RAM, but we also have some other stuff, like a
  //   terminal. We choose certain address ranges to correspond
  //   to certain components, and we manage the reads and writes
  //   to them.
  //   To complicate things a little bit, we don't just need to be able
  //   to read and write for loads and stores. We also need to be able
  //   to read out instructions and support any accesses the debug
  //   module needs to do. This is why we have three address inputs,
  //   three data outputs, and three sets of control signals.
  //   This is where the debug module writes and branches to when
  //   it wants to execute arbitrary code. It's split into pieces because
  //   it is read by three things: the debug module, the instruction
  //   decoder, and instruction execution.
  //   This is the only location in memory other than progbuf that the
  //   debug module can read and write to. Oftentimes it's used in
  //   conjunction with progbuf to move data in and out of memory.
  //   Outputs
  //   We select where to take the various read values from based on
  //   what ranges our addresses are in.
endmodule
