// Digital circuit RV5-IMM-GEN.dig as structural Verilog
module RV5_IMM_GEN (
  input  [31:0] inst,
  input  [2:0] imm_sel,
  output [31:0] out
);

  wire [31:0] imm_b, imm_i, imm_j, imm_s;

  BitExtender #(.inputBits(21), .outputBits(32)) bitextender_1 (
    .in({inst[31], inst[19:12], inst[20], inst[30:21], 1'b0}), .out(imm_j));
  BitExtender #(.inputBits(12), .outputBits(32)) bitextender_2 (.in({inst[31:25], inst[11:7]}), .out(imm_s));
  Multiplexer #(.Selector_Bits(3), .Bits(32)) multiplexer_1 (
    .sel(imm_sel), .in_0(imm_i), .in_1(imm_s), .in_2(imm_b), .in_3({inst[31:12], {12{1'b0}}}), .in_4(imm_j),
    .in_5({32{1'b0}}), .in_6({32{1'b0}}), .in_7({32{1'b0}}), .out(out));
  BitExtender #(.inputBits(13), .outputBits(32)) bitextender_3 (
    .in({inst[31], inst[7], inst[30:25], inst[11:8], 1'b0}), .out(imm_b));
  BitExtender #(.inputBits(12), .outputBits(32)) bitextender_4 (.in(inst[31:20]), .out(imm_i));

  // Other names for the same wires on the sheet: imm_signext[31:0] = out; imm_u[31:12] = inst[31:12]

  // Notes on the sheet:
  //   inst: default 33621011
  //   RV5-IMM-GEN
  //   Different instruction types have different layouts, 
  //   so we need different logic to extract the immediates.
  //   Additionally, all but U-type instruction immediates
  //   need to be sign-extended.
  //   Immediate extract split sign-extend
  //   Immediate Selector MUX
endmodule
