// Digital circuit RV5-MEMORY.dig as structural Verilog
module RV5_MEMORY (
  input  [31:0] addr,
  input  [31:0] wdata,
  input  wen,
  input  ren,
  input  clk,
  input  \byte ,
  input  half,
  input  signext,
  input  [31:0] inst_addr,
  input  [31:0] dm_addr,
  input  dm_wen,
  input  [31:0] dm_wdata,
  output [31:0] out,
  output [31:0] inst_out,
  output [31:0] dm_out
);

  wire addr_data0, addr_filemap, addr_progbuf_0, addr_progbuf_1, addr_progbuf_2, addr_progbuf_3,
       addr_progbuf_4, addr_progbuf_5, addr_progbuf_6, addr_progbuf_7, addr_ram, addr_terminal, and_1_out,
       and_2_out, and_3_out, and_4_out, and_5_out, and_6_out, and_7_out, and_8_out, and_9_out, and_10_out,
       and_11_out, and_12_out, and_13_out, and_14_out, dm_addr_data0, dm_addr_progbuf_0, dm_addr_progbuf_1,
       dm_addr_progbuf_2, dm_addr_progbuf_3, dm_addr_progbuf_4, dm_addr_progbuf_5, dm_addr_progbuf_6,
       dm_addr_progbuf_7, dm_addr_ram, filemap_inst, inst_addr_data0, inst_addr_filemap, inst_addr_progbuf_0,
       inst_addr_progbuf_1, inst_addr_progbuf_2, inst_addr_progbuf_3, inst_addr_progbuf_4,
       inst_addr_progbuf_5, inst_addr_progbuf_6, inst_addr_progbuf_7, inst_addr_ram, inst_addr_terminal,
       interactiveterminal_1_p6, or_1_out, or_2_out;
  wire [15:0] interactiveterminal_1_p5, terminal;
  wire [31:0] data0, filemap, filemapper_1_p7, masked_overlay_1_out, masked_overlay_2_out, multiplexer_2_out,
       progbuf_0, progbuf_1, progbuf_2, progbuf_3, progbuf_4, progbuf_5, progbuf_6, progbuf_7, ram, RAM_d1,
       ram_inst, sub_1_s, sub_2_s;

  MASKED_OVERLAY masked_overlay_1 (
    .base(RAM_d1), .data(wdata), .addr(addr), .\byte (\byte ), .half(half), .out(masked_overlay_1_out));
  and and_1 (and_1_out, wen, addr_ram);
  and and_2 (and_2_out, addr_terminal, wen);
  and and_3 (and_3_out, addr_terminal, ren);
  RAMDualAccess #(.AddrBits(24), .isProgramMemory("true"), .Bits(32)) u_RAM (
    .str(and_1_out), .C(clk), .ld(addr_ram), .A1(addr[25:2]), .Din1(masked_overlay_1_out),
    .A2(inst_addr[25:2]), .D1(RAM_d1), .D2(ram_inst));
  // InteractiveTerminal interactiveterminal_1: pin names not known; wires that end beside it: wdata, and_2_out, and_3_out, clk, interactiveterminal_1_p5, interactiveterminal_1_p6
  // AddressDecoder #(.addressDecoderRules("0x418 : addr-data0\n0x10000 : addr-terminal\n0x10004..0x10020/4 : addr-progbuf\n>0x3FFFFFF : addr-filemap\n* : addr-ram"), .Bits(32)) addressdecoder_1: pin names not known; wires that end beside it: addr, addr_data0, addr_terminal, addr_progbuf_0, addr_progbuf_1, addr_progbuf_2, addr_progbuf_3, addr_progbuf_4, addr_progbuf_5, addr_progbuf_6, addr_progbuf_7, addr_filemap, addr_ram
  Multiplexer #(.Bits(16)) multiplexer_1 (
    .sel(interactiveterminal_1_p6), .in_0(16'h4), .in_1(interactiveterminal_1_p5), .out(terminal));
  ISOLATE_SIGNEXT isolate_signext_1 (
    .data(RAM_d1), .addr(addr), .\byte (\byte ), .half(half), .signext(signext), .out(ram));
  // AddressDecoder #(.addressDecoderRules("0x418 : addr-data0\n0x10000 : addr-terminal\n0x10004..0x10020/4 : addr-progbuf\n>0x3FFFFFF : addr-filemap\n* : addr-ram"), .Bits(32)) addressdecoder_2: pin names not known; wires that end beside it: dm_addr, dm_addr_data0, dm_addr_progbuf_0, dm_addr_progbuf_1, dm_addr_progbuf_2, dm_addr_progbuf_3, dm_addr_progbuf_4, dm_addr_progbuf_5, dm_addr_progbuf_6, dm_addr_progbuf_7, dm_addr_ram
  Sub #(.Bits(32)) sub_1 (.a(addr), .b(32'h4000000), .c_i(1'b0), .s(sub_1_s));  // open: c_o
  Sub #(.Bits(32)) sub_2 (.a(inst_addr), .b(32'h4000000), .c_i(1'b0), .s(sub_2_s));  // open: c_o
  and and_4 (and_4_out, addr_filemap, wen);
  or or_1 (or_1_out, addr_filemap, inst_addr_filemap);
  MASKED_OVERLAY masked_overlay_2 (
    .base(filemapper_1_p7), .data(wdata), .addr(addr), .\byte (\byte ), .half(half),
    .out(masked_overlay_2_out));
  // AddressDecoder #(.addressDecoderRules("0x418 : addr-data0\n0x10000 : addr-terminal\n0x10004..0x10020/4 : addr-progbuf\n>0x3FFFFFF : addr-filemap\n* : addr-ram"), .Bits(32)) addressdecoder_3: pin names not known; wires that end beside it: inst_addr, inst_addr_data0, inst_addr_terminal, inst_addr_progbuf_0, inst_addr_progbuf_1, inst_addr_progbuf_2, inst_addr_progbuf_3, inst_addr_progbuf_4, inst_addr_progbuf_5, inst_addr_progbuf_6, inst_addr_progbuf_7, inst_addr_filemap, inst_addr_ram
  // FileMapper #(.Bits(32)) filemapper_1: pin names not known; wires that end beside it: {2'b00, sub_1_s[31:2]}, {2'b00, sub_2_s[31:2]}, masked_overlay_2_out, and_4_out, or_1_out, clk, filemapper_1_p7, filemap_inst
  ISOLATE_SIGNEXT isolate_signext_2 (
    .data(filemapper_1_p7), .addr(addr), .\byte (\byte ), .half(half), .signext(signext), .out(filemap));
  and and_5 (and_5_out, dm_addr_data0, dm_wen);
  and and_6 (and_6_out, addr_data0, wen);
  and and_7 (and_7_out, dm_addr_progbuf_0, dm_wen);
  and and_8 (and_8_out, dm_addr_progbuf_1, dm_wen);
  and and_9 (and_9_out, dm_addr_progbuf_2, dm_wen);
  and and_10 (and_10_out, dm_addr_progbuf_3, dm_wen);
  and and_11 (and_11_out, dm_addr_progbuf_4, dm_wen);
  and and_12 (and_12_out, dm_addr_progbuf_5, dm_wen);
  and and_13 (and_13_out, dm_addr_progbuf_6, dm_wen);
  and and_14 (and_14_out, dm_addr_progbuf_7, dm_wen);
  Register #(.Bits(32)) u_progbuf_0 (.D(dm_wdata), .C(clk), .en(and_7_out), .Q(progbuf_0));
  Register #(.Bits(32)) u_progbuf_1 (.D(dm_wdata), .C(clk), .en(and_8_out), .Q(progbuf_1));
  Register #(.Bits(32)) u_progbuf_2 (.D(dm_wdata), .C(clk), .en(and_9_out), .Q(progbuf_2));
  Register #(.Bits(32)) u_progbuf_3 (.D(dm_wdata), .C(clk), .en(and_10_out), .Q(progbuf_3));
  Register #(.Bits(32)) u_progbuf_4 (.D(dm_wdata), .C(clk), .en(and_11_out), .Q(progbuf_4));
  Register #(.Bits(32)) u_progbuf_5 (.D(dm_wdata), .C(clk), .en(and_12_out), .Q(progbuf_5));
  Register #(.Bits(32)) u_progbuf_6 (.D(dm_wdata), .C(clk), .en(and_13_out), .Q(progbuf_6));
  Register #(.Bits(32)) u_progbuf_7 (.D(dm_wdata), .C(clk), .en(and_14_out), .Q(progbuf_7));
  Multiplexer #(.Bits(32)) multiplexer_2 (.sel(and_5_out), .in_0(wdata), .in_1(dm_wdata), .out(multiplexer_2_out));
  or or_2 (or_2_out, and_5_out, and_6_out);
  Register #(.Bits(32)) u_data0 (.D(multiplexer_2_out), .C(clk), .en(or_2_out), .Q(data0));
  // OneHotMultiplexer #(.Bits(32)) onehotmultiplexer_1: pin names not known; wires that end beside it: addr_ram, addr_terminal, addr_progbuf_0, addr_progbuf_1, addr_progbuf_2, addr_progbuf_3, addr_progbuf_4, addr_progbuf_5, addr_progbuf_6, addr_progbuf_7, addr_data0, addr_filemap, ram, {{16{1'b0}}, terminal}, progbuf_0, progbuf_1, progbuf_2, progbuf_3, progbuf_4, out
  // OneHotMultiplexer #(.Bits(32)) onehotmultiplexer_2: pin names not known; wires that end beside it: progbuf_5, progbuf_6, progbuf_7, data0, filemap, inst_addr_ram, inst_addr_progbuf_0, inst_addr_progbuf_1, inst_addr_progbuf_2, inst_addr_progbuf_3, inst_addr_progbuf_4, inst_addr_progbuf_5, inst_addr_progbuf_6, inst_addr_progbuf_7, inst_addr_data0, inst_addr_filemap, ram_inst, progbuf_0, progbuf_1, progbuf_2, progbuf_3, progbuf_4, progbuf_5, inst_out
  // OneHotMultiplexer #(.Bits(32)) onehotmultiplexer_3: pin names not known; wires that end beside it: progbuf_6, progbuf_7, data0, filemap_inst, dm_addr_progbuf_0, dm_addr_progbuf_1, dm_addr_progbuf_2, dm_addr_progbuf_3, dm_addr_progbuf_4, dm_addr_progbuf_5, dm_addr_progbuf_6, dm_addr_progbuf_7, dm_addr_data0, progbuf_0, progbuf_1, progbuf_2, progbuf_3, progbuf_4, progbuf_5, progbuf_6, progbuf_7, data0, dm_out

  // Notes on the sheet:
  //   RV5-MEMORY
  //   Inputs
  //   All of our inputs!
  //   Memory-Mapped Items
  //   RAM
  //   This is a dual-port RAM. It supports reading and writing at address 1A
  //   and reading at address 1B. I'm using 1A for instruction operations and
  //   1B for instruction reads.
  //   Terminal
  //   This is the terminal! We can read and write characters! Character input
  //   is queued, and a value of 4 (EOT in ASCII) means there is currently
  //   nothing left.
  //   If we're writing a half or byte, we
  //   need to take the remaining bytes
  //   of the old word and merge them
  //   with our new bytes.
  //   Address Control Signals
  //   We determine which devices are currently being addressed.
  //   What is the main data address pointing to?
  //   We might need to sign extend.
  //   Additionally, if we're reading a byte
  //   or a half, we need to isolate that
  //   value from the rest of the word.
  //   What is the debug module trying to look at?
  //   These are equivilent
  //   to RV5-MEM-ADDR-DECODE
  //   (but faster in the sim).
  //   Mapped File
  //   This component has an interface for controlling file mapping (at relative
  //   address 0x0) and potentially a mapped file (at relative address 0x1000).
  //   The contents can be executed.
  //   What is the main instruction address pointing to?
  //   Program Buffer
  //   This is where the debug module writes and branches to when
  //   it wants to execute arbitrary code. It's split into pieces because
  //   it is read by three things: the debug module, the instruction
  //   decoder, and instruction execution.
  //   data0
  //   This is the only location in memory other than progbuf that the
  //   debug module can read and write to. Oftentimes it's used in
  //   conjunction with progbuf to move data in and out of memory.
  //   Understanding the Memory
  //   This is a memory module with a few items mapped. Of course,
  //   we have RAM, but we also have some other stuff, like a
  //   terminal. We choose certain address ranges to correspond
  //   to certain components, and we manage the reads and writes
  //   to them.
  //   To complicate things a little bit, we don't just need to be able
  //   to read and write for loads and stores. We also need to be able
  //   to read out instructions and support any accesses the debug
  //   module needs to do. This is why we have three address inputs,
  //   three data outputs, and three sets of control signals.
  //   Note:
  //   Technically, we should
  //   support half and byte
  //   accesses to these. Maybe at
  //   some point we will.
  //   It's pretty non-essential.
  //   Outputs
  //   We select where to take the various 
  //   read values from based on what
  //   ranges our addresses are in.
  //   These are just sum-of-product
  //   selectors:
  //   (Like ONE-HOT-SEL-32x12 but
  //   more performant in the sim.)
  //   (Like ONE-HOT-SEL-32x11 but
  //   more performant in the sim.)
  //   (Like ONE-HOT-SEL-32x9 but
  //   more performant in the sim.)
endmodule
