// Digital circuit ONE-HOT-SEL-32x12.dig as structural Verilog
module ONE_HOT_SEL_32x12 (
  input  [31:0] _0,
  input  _0_sel,
  input  [31:0] _1,
  input  _1_sel,
  input  [31:0] _2,
  input  _2_sel,
  input  [31:0] _3,
  input  _3_sel,
  input  [31:0] _4,
  input  _4_sel,
  input  [31:0] _5,
  input  _5_sel,
  input  [31:0] _6,
  input  _6_sel,
  input  [31:0] _7,
  input  _7_sel,
  input  [31:0] _8,
  input  _8_sel,
  input  [31:0] _9,
  input  _9_sel,
  input  [31:0] _10,
  input  _10_sel,
  input  [31:0] _11,
  input  _11_sel,
  output [31:0] out
);

  assign out = _0_sel ? _0 : 32'bz;  // Driver driver_1
  assign out = _1_sel ? _1 : 32'bz;  // Driver driver_2
  assign out = _2_sel ? _2 : 32'bz;  // Driver driver_3
  assign out = _3_sel ? _3 : 32'bz;  // Driver driver_4
  assign out = _4_sel ? _4 : 32'bz;  // Driver driver_5
  assign out = _5_sel ? _5 : 32'bz;  // Driver driver_6
  assign out = _6_sel ? _6 : 32'bz;  // Driver driver_7
  assign out = _7_sel ? _7 : 32'bz;  // Driver driver_8
  assign out = _8_sel ? _8 : 32'bz;  // Driver driver_9
  assign out = _9_sel ? _9 : 32'bz;  // Driver driver_10
  assign out = _10_sel ? _10 : 32'bz;  // Driver driver_11
  assign out = _11_sel ? _11 : 32'bz;  // Driver driver_12

  // Notes on the sheet:
  //   ONE-HOT-SEl-32x12
endmodule
