// Digital circuit ONE-HOT-SEL-32x5.dig as structural Verilog
module ONE_HOT_SEL_32x5 (
  input  [31:0] _0,
  input  _0_sel,
  input  [31:0] _1,
  input  _1_sel,
  input  [31:0] _2,
  input  _2_sel,
  input  [31:0] _3,
  input  _3_sel,
  input  [31:0] _4,
  input  _4_sel,
  output [31:0] out
);

  assign out = _0_sel ? _0 : 32'bz;  // Driver driver_1
  assign out = _1_sel ? _1 : 32'bz;  // Driver driver_2
  assign out = _2_sel ? _2 : 32'bz;  // Driver driver_3
  assign out = _3_sel ? _3 : 32'bz;  // Driver driver_4
  assign out = _4_sel ? _4 : 32'bz;  // Driver driver_5

  // Notes on the sheet:
  //   ONE-HOT-SEl-32x5
endmodule
